// Logisim project Controlador.circ as structural Verilog: 1 circuit, main circuit main
// 8
module main (
  input  [7:0] PC,
  input  [7:0] AB,
  input  PEGA_PC,
  input  LDA,
  input  STA
);

  wire and_2_out, clock_1_out, not_1_out, Pega;
  wire [0:0] and_1_out;
  wire [7:0] AB_t, \Endereço , \Instrução ;
  wire [15:0] Acc, setAcc, setIR, transistor_1_out, Valor;

  Clock clock_1 (.out(clock_1_out));
  Register #(.width(16)) IR (.D(setIR), .en(PEGA_PC), .Q({AB_t, \Instrução }), .clk(clock_1_out), .clr(1'b0));
  not not_1 (not_1_out, PEGA_PC);
  Multiplexer #(.select(2), .width(8), .enable("false")) multiplexer_1 (
    .in0(PC), .in1(AB_t), .in2(AB), .out(\Endereço ), .sel({STA, and_1_out[0]}));  // open: in3
  and and_1 (and_1_out[0], LDA, not_1_out);
  Demultiplexer #(.width(16), .enable("false")) demultiplexer_1 (
    .out0(setIR), .out1(setAcc), .in(Valor), .sel(and_1_out[0]));
  Register #(.width(16)) Acumulador (.D(setAcc), .en(LDA), .Q(Acc), .clk(clock_1_out), .clr(1'b0));
  and and_2 (and_2_out, clock_1_out, STA);
  or or_1 (Pega, PEGA_PC, LDA);
  Transistor #(.\type ("n"), .width(16)) transistor_1 (.in(Acc), .out(transistor_1_out), .gate(STA));
  RAM #(.dataWidth(16)) ram_1 (
    .addr(\Endereço ), .data(transistor_1_out), .sel(1'b1), .clk(and_2_out), .ld(Pega), .clr(1'b0));
  Transistor #(.\type ("n"), .width(16)) transistor_2 (.in(transistor_1_out), .out(Valor), .gate(Pega));
endmodule
